// Logisim project 1.circ as structural Verilog: 2 circuits, main circuit alu8
module alu8 (
  input  [7:0] a,
  input  [7:0] b,
  input  [3:0] op,
  output [7:0] rddata
);

  wire alu_1_cout, comparator_1_eq, multiplexer_2_out;
  wire [3:0] aluout1, aluout2;
  wire [7:0] and_1_out, bit_extender_1_out, not_1_out, or_1_out, shifter_1_out, shifter_2_out, xor_1_out;

  assign or_1_out = a | b;  // OR_Gate or_1, 8 bits wide
  assign and_1_out = b & a;  // AND_Gate and_1, 8 bits wide
  assign xor_1_out = b ^ a;  // XOR_Gate xor_1, 8 bits wide
  Comparator comparator_1 (.a(a), .b(b), .eq(comparator_1_eq));  // open: gt, lt
  assign not_1_out = ~a;  // NOT_Gate not_1, 8 bits wide
  assign bit_extender_1_out = {{7{1'b0}}, comparator_1_eq};  // Bit_Extender bit_extender_1
  Shifter #(.shift("lr")) shifter_1 (.in(a), .\dist (3'b001), .out(shifter_1_out));
  Shifter shifter_2 (.in(a), .\dist (3'b001), .out(shifter_2_out));
  Multiplexer #(.select(4), .width(8), .enable("false")) multiplexer_1 (
    .in1(not_1_out), .in2(and_1_out), .in3(xor_1_out), .in4(or_1_out), .in5({aluout2, aluout1}),
    .in6({aluout2, aluout1}), .in7(a), .in8(b), .in9({aluout2, aluout1}), .in10({aluout2, aluout1}),
    .in11(shifter_2_out), .in12(shifter_1_out), .in13(bit_extender_1_out), .out(rddata), .sel(op));  // open: in0, in14, in15
  Multiplexer #(.enable("false")) multiplexer_2 (.in0(1'b0), .in1(1'b1), .out(multiplexer_2_out), .sel(op[1]));
  alu alu_1 (
    .inputa(a[3:0]), .inputb(b[3:0]), .operation(op), .carryin(multiplexer_2_out), .aluout(aluout1),
    .cout(alu_1_cout));
  alu alu_2 (.inputa(a[7:4]), .inputb(b[7:4]), .operation(op), .carryin(alu_1_cout), .aluout(aluout2));  // open: cout

  // Other names for the same wires on the sheet: a4bit1[3:0] = a[3:0]; aInput[7:0] = a; a4bit2[3:0] = a[7:4];
  //   b4bit1[3:0] = b[3:0]; bInput[7:0] = b; b4bit2[3:0] = b[7:4]; CLAOUT[7:0] = {aluout2, aluout1}; opbits[3:0] = op;
  //   outputData[7:0] = rddata
endmodule

module alu (
  input  [3:0] inputa,
  input  [3:0] inputb,
  input  [3:0] operation,
  input  carryin,
  output [3:0] aluout,
  output cout
);

  wire and_1_out, and_2_out, and_3_out, and_4_out, and_5_out, and_6_out, and_11_out, and_12_out, and_13_out,
       and_14_out, c1, c2, c3, g0, g1, g2, g3, multiplexer_1_out, multiplexer_2_out, multiplexer_3_out,
       multiplexer_4_out, multiplexer_5_out, multiplexer_6_out, multiplexer_7_out, multiplexer_8_out,
       multiplexer_9_out, multiplexer_10_out, multiplexer_11_out, multiplexer_12_out, not_1_out, not_2_out,
       not_3_out, not_4_out, not_5_out, not_6_out, not_7_out, not_8_out, not_9_out, not_10_out, not_11_out,
       not_12_out, p0, p1, p2, p3, xor_5_out, xor_6_out, xor_7_out, xor_8_out, xor_9_out, xor_10_out,
       xor_11_out, xor_12_out;

  and and_1 (and_1_out, p0, carryin);
  and and_2 (and_2_out, g0, p1);
  and and_3 (and_3_out, p0, p1, carryin);
  and and_4 (and_4_out, g1, p2);
  and and_5 (and_5_out, g0, p1, p2);
  and and_6 (and_6_out, p0, p1, p2, carryin);
  not not_1 (not_1_out, inputb[0]);
  not not_2 (not_2_out, inputb[0]);
  not not_3 (not_3_out, inputb[1]);
  not not_4 (not_4_out, inputb[1]);
  not not_5 (not_5_out, inputb[2]);
  not not_6 (not_6_out, inputb[2]);
  not not_7 (not_7_out, inputb[3]);
  not not_8 (not_8_out, inputb[3]);
  or or_1 (c1, g0, and_1_out);
  or or_2 (c2, g1, and_2_out, and_3_out);
  or or_3 (c3, g2, and_4_out, and_5_out, and_6_out);
  Multiplexer #(.enable("false")) multiplexer_1 (
    .in0(inputb[0]), .in1(not_1_out), .out(multiplexer_1_out), .sel(operation[1]));
  and and_7 (g0, multiplexer_1_out, inputa[0]);
  Multiplexer #(.enable("false")) multiplexer_2 (
    .in0(inputb[0]), .in1(not_2_out), .out(multiplexer_2_out), .sel(operation[1]));
  Multiplexer #(.enable("false")) multiplexer_3 (
    .in0(inputb[1]), .in1(not_3_out), .out(multiplexer_3_out), .sel(operation[1]));
  and and_8 (g1, multiplexer_3_out, inputa[1]);
  Multiplexer #(.enable("false")) multiplexer_4 (
    .in0(inputb[1]), .in1(not_4_out), .out(multiplexer_4_out), .sel(operation[1]));
  Multiplexer #(.enable("false")) multiplexer_5 (
    .in0(inputb[2]), .in1(not_5_out), .out(multiplexer_5_out), .sel(operation[1]));
  and and_9 (g2, multiplexer_5_out, inputa[2]);
  Multiplexer #(.enable("false")) multiplexer_6 (
    .in0(inputb[2]), .in1(not_6_out), .out(multiplexer_6_out), .sel(operation[1]));
  Multiplexer #(.enable("false")) multiplexer_7 (
    .in0(inputb[3]), .in1(not_7_out), .out(multiplexer_7_out), .sel(operation[1]));
  and and_10 (g3, multiplexer_7_out, inputa[3]);
  Multiplexer #(.enable("false")) multiplexer_8 (
    .in0(inputb[3]), .in1(not_8_out), .out(multiplexer_8_out), .sel(operation[1]));
  xor xor_1 (p0, multiplexer_2_out, inputa[0]);
  xor xor_2 (p1, multiplexer_4_out, inputa[1]);
  xor xor_3 (p2, multiplexer_6_out, inputa[2]);
  xor xor_4 (p3, multiplexer_8_out, inputa[3]);
  and and_11 (and_11_out, g2, p3);
  and and_12 (and_12_out, g1, p2, p3);
  and and_13 (and_13_out, g0, p1, p2, p3);
  and and_14 (and_14_out, p0, p1, p2, p3, carryin);
  or or_4 (cout, g3, and_11_out, and_12_out, and_13_out, and_14_out);
  not not_9 (not_9_out, inputb[0]);
  not not_10 (not_10_out, inputb[1]);
  not not_11 (not_11_out, inputb[2]);
  not not_12 (not_12_out, inputb[3]);
  Multiplexer #(.enable("false")) multiplexer_9 (
    .in0(inputb[0]), .in1(not_9_out), .out(multiplexer_9_out), .sel(operation[1]));
  xor xor_5 (xor_5_out, multiplexer_9_out, inputa[0]);
  Multiplexer #(.enable("false")) multiplexer_10 (
    .in0(inputb[1]), .in1(not_10_out), .out(multiplexer_10_out), .sel(operation[1]));
  Multiplexer #(.enable("false")) multiplexer_11 (
    .in0(inputb[2]), .in1(not_11_out), .out(multiplexer_11_out), .sel(operation[1]));
  xor xor_6 (xor_6_out, multiplexer_11_out, inputa[2]);
  Multiplexer #(.enable("false")) multiplexer_12 (
    .in0(inputb[3]), .in1(not_12_out), .out(multiplexer_12_out), .sel(operation[1]));
  xor xor_7 (xor_7_out, multiplexer_12_out, inputa[3]);
  xor xor_8 (xor_8_out, xor_5_out, carryin);
  xor xor_9 (xor_9_out, multiplexer_10_out, inputa[1]);
  xor xor_10 (xor_10_out, xor_9_out, c1);
  xor xor_11 (xor_11_out, xor_6_out, c2);
  xor xor_12 (xor_12_out, xor_7_out, c3);
  Multiplexer #(.select(4), .enable("false")) multiplexer_13 (
    .in5(xor_8_out), .in6(xor_8_out), .in9(xor_8_out), .in10(xor_8_out), .out(aluout[0]), .sel(operation));  // open: in0, in1, in2, in3, in4, in7, in8, in11, in12, in13, in14, in15
  Multiplexer #(.select(4), .enable("false")) multiplexer_14 (
    .in5(xor_10_out), .in6(xor_10_out), .in9(xor_10_out), .in10(xor_10_out), .out(aluout[1]), .sel(operation));  // open: in0, in1, in2, in3, in4, in7, in8, in11, in12, in13, in14, in15
  Multiplexer #(.select(4), .enable("false")) multiplexer_15 (
    .in5(xor_11_out), .in6(xor_11_out), .in9(xor_11_out), .in10(xor_11_out), .out(aluout[2]), .sel(operation));  // open: in0, in1, in2, in3, in4, in7, in8, in11, in12, in13, in14, in15
  Multiplexer #(.select(4), .enable("false")) multiplexer_16 (
    .in5(xor_12_out), .in6(xor_12_out), .in9(xor_12_out), .in10(xor_12_out), .out(aluout[3]), .sel(operation));  // open: in0, in1, in2, in3, in4, in7, in8, in11, in12, in13, in14, in15
  // Probe on operation
  // Probe on operation
  // Probe on operation
  // Probe on operation
  // Probe on aluout

  // Other names for the same wires on the sheet: cin = carryin; a0 = inputa[0]; a1 = inputa[1]; a2 = inputa[2];
  //   a3 = inputa[3]; b0 = inputb[0]; b1 = inputb[1]; b2 = inputb[2]; b3 = inputb[3]; opbits[3:0] = operation;
  //   alu0 = aluout[0]; outputALU[3:0] = aluout; alu1 = aluout[1]; alu2 = aluout[2]; alu3 = aluout[3]
endmodule
