// Logisim project 2.circ as structural Verilog: 1 circuit, main circuit instructions
module instructions (
  input  resetall,
  input  sysclock,
  output [7:0] pc,
  output [3:0] op,
  output [2:0] rd,
  output [2:0] rs1,
  output [2:0] rs2,
  output [7:0] imm
);

  Counter counter_1 (.clr(resetall), .clk(sysclock), .Q(pc));  // open: load, up, count, D, carry
  RAM #(.dataWidth(21)) ram_1 (.addr(pc), .we(1'b0), .oe(1'b1), .clk(sysclock), .data({op, rd, rs1, rs2, imm}));

  // Other names for the same wires on the sheet: immbin[7:0] = imm; rs2bin[2:0] = rs2; rs1bin[2:0] = rs1;
  //   rdbin[2:0] = rd; opcode[3:0] = op; pco[7:0] = pc; sysc = sysclock
endmodule
