// Logisim project 3.circ as structural Verilog: 1 circuit, main circuit regfile
module regfile (
  input  [2:0] rd,
  input  [7:0] rddata,
  input  wen,
  input  resetall,
  input  sysclock,
  output [7:0] x0,
  output [7:0] x1,
  output [7:0] x2,
  output [7:0] x3,
  output [7:0] x4,
  output [7:0] x5,
  output [7:0] x6,
  output [7:0] x7
);

  wire r0, r1, r2, r3, r4, r5, r6, r7;

  Decoder #(.select(3)) decoder_1 (
    .out0(r0), .out1(r1), .out2(r2), .out3(r3), .out4(r4), .out5(r5), .out6(r6), .out7(r7), .sel(rd), .en(wen));
  Register register_1 (.D(rddata), .en(r0), .clk(sysclock), .Q(x0), .clr(resetall));
  Register register_2 (.D(rddata), .en(r1), .clk(sysclock), .Q(x1), .clr(resetall));
  Register register_3 (.D(rddata), .en(r2), .clk(sysclock), .Q(x2), .clr(resetall));
  Register register_4 (.D(rddata), .en(r3), .clk(sysclock), .Q(x3), .clr(resetall));
  Register register_5 (.D(rddata), .en(r4), .clk(sysclock), .Q(x4), .clr(resetall));
  Register register_6 (.D(rddata), .en(r5), .clk(sysclock), .Q(x5), .clr(resetall));
  Register register_7 (.D(rddata), .en(r6), .clk(sysclock), .Q(x6), .clr(resetall));
  Register register_8 (.D(rddata), .en(r7), .clk(sysclock), .Q(x7), .clr(resetall));

  // Other names for the same wires on the sheet: rdbits[2:0] = rd; rdd[7:0] = rddata; reset = resetall;
  //   sysc = sysclock; we = wen; x0o[7:0] = x0; x1o[7:0] = x1; x2o[7:0] = x2; x3o[7:0] = x3; x4o[7:0] = x4;
  //   x5o[7:0] = x5; x6o[7:0] = x6; x7o[7:0] = x7
endmodule
